// Logisim project dram.circ as structural Verilog: 2 circuits, main circuit main
module main (
  input  [23:0] ADDR,
  input  [15:0] DATA,
  input  AS_,
  input  CS_,
  input  WR_
);

  wire and_1_out, and_2_out, CAS_REFR_, CLK20, d_ff_1_q, d_ff_3_q, d_ff_3_qn, d_ff_4_q, d_ff_4_qn, EN_,
       nand_1_out, not_1_out, not_2_out, not_3_out, RAS_REFR_;

  Clock u_CLK20 (.out(CLK20));
  nand nand_1 (nand_1_out, CAS_REFR_, RAS_REFR_);
  not not_1 (not_1_out, EN_);
  not not_2 (not_2_out, EN_);
  or or_1 (EN_, AS_, CS_, nand_1_out);
  and and_1 (and_1_out, d_ff_4_qn, CLK20, not_1_out);
  D_Flip_Flop d_ff_1 (.D(RAS_REFR_), .clk(CLK20), .Q(d_ff_1_q), .Qn(CAS_REFR_), .reset(not_2_out));  // open: preset
  D_Flip_Flop d_ff_2 (.D(d_ff_1_q), .clk(CLK20), .Qn(RAS_REFR_), .reset(not_2_out));  // open: Q, preset
  not not_3 (not_3_out, not_1_out);
  // Probe on CAS_REFR_
  // Probe on RAS_REFR_
  D_Flip_Flop d_ff_3 (.D(d_ff_4_qn), .clk(and_1_out), .Q(d_ff_3_q), .Qn(d_ff_3_qn), .reset(not_3_out));  // open: preset
  D_Flip_Flop d_ff_4 (.D(d_ff_3_q), .clk(and_1_out), .Q(d_ff_4_q), .Qn(d_ff_4_qn), .reset(not_3_out));  // open: preset
  and and_2 (and_2_out, d_ff_3_qn, d_ff_4_qn);
  // Probe on and_2_out
  // Probe on d_ff_4_qn
  // Probe on d_ff_4_q
endmodule

module SIMM8MB (
  input  [9:0] ADDR,
  input  RAS0_60c01c3d,
  input  RAS1_0dbaec86,
  input  RAS2_75fc2df1,
  input  RAS3_7f50937e,
  input  CAS0_f09fe7b2,
  input  CAS1_00002722,
  input  CAS2_3977e826,
  input  CAS3_af8aeb87,
  input  WE_98a5766a,
  input  [31:0] DATAIN,
  output [31:0] DATAOUT
);

  wire and_1_out, and_2_out, not_1_out;
  wire [9:0] register_1_q, register_2_q;

  and and_1 (and_1_out, RAS0_60c01c3d, RAS1_0dbaec86, RAS2_75fc2df1, RAS3_7f50937e);
  Register #(.width(10), .trigger("falling")) register_1 (
    .D(ADDR), .en(1'b1), .clk(and_1_out), .Q(register_1_q));  // open: clr
  and and_2 (and_2_out, CAS0_f09fe7b2, CAS1_00002722, CAS2_3977e826, CAS3_af8aeb87);
  not not_1 (not_1_out, WE_98a5766a);
  Register #(.width(10), .trigger("falling")) register_2 (
    .D(ADDR), .en(1'b1), .clk(and_2_out), .Q(register_2_q));  // open: clr
  RAM #(.addrWidth(20)) ram_1 (
    .addr({register_1_q, register_2_q}), .we(not_1_out), .oe(WE_98a5766a), .data(DATAIN[7:0]));  // open: clk
  RAM #(.addrWidth(20)) ram_2 (
    .addr({register_1_q, register_2_q}), .we(not_1_out), .oe(WE_98a5766a), .data(DATAIN[23:16]));  // open: clk
  RAM #(.addrWidth(20)) ram_3 (
    .addr({register_1_q, register_2_q}), .we(not_1_out), .oe(WE_98a5766a), .data(DATAIN[7:0]));  // open: clk
  RAM #(.addrWidth(20)) ram_4 (
    .addr({register_1_q, register_2_q}), .we(not_1_out), .oe(WE_98a5766a), .data(DATAIN[23:16]));  // open: clk
  RAM #(.addrWidth(20)) ram_5 (
    .addr({register_1_q, register_2_q}), .we(not_1_out), .oe(WE_98a5766a), .data(DATAIN[15:8]));  // open: clk
  RAM #(.addrWidth(20)) ram_6 (
    .addr({register_1_q, register_2_q}), .we(not_1_out), .oe(WE_98a5766a), .data(DATAIN[31:24]));  // open: clk
  RAM #(.addrWidth(20)) ram_7 (
    .addr({register_1_q, register_2_q}), .we(not_1_out), .oe(WE_98a5766a), .data(DATAIN[15:8]));  // open: clk
  RAM #(.addrWidth(20)) ram_8 (
    .addr({register_1_q, register_2_q}), .we(not_1_out), .oe(WE_98a5766a), .data(DATAIN[31:24]));  // open: clk

  assign DATAOUT = DATAIN;
endmodule
